// Logisim project main.circ as structural Verilog
module main (
  input  in_1
);

  wire and_1_out, chGM, End_of_printing, gS0, gS1, gS2, InpFl, letsPrint, LoadMap, mainClk, mainRES,
       not_1_out, not_2_out, not_3_out, not_4_out, register_2_q, register_3_q, StateCh;
  wire [3:0] gameState, gSto;
  wire [7:0] gStdtScrMem, InpKey, maps_1_data, maps_1_out_3, maps_1_out_4, memChar,
       printing_map_1_mem_to_display, Xpp_q, Ypp_q;
  wire [11:0] mapH_q, maps_1_height, maps_1_width, mapW_q, memN, printing_map_1_addr_on_display,
       printing_map_1_curr_adr_in_map, tpLen;

  or or_1 (letsPrint, in_1, gS0);
  Clock clock_1 (.out(mainClk));
  Button button_1 (.out(mainRES));
  Register Xpp (.D(maps_1_out_3), .Q(Xpp_q), .clr(LoadMap));  // open: en, clk
  Register #(.width(12)) mapW (.D(maps_1_width), .Q(mapW_q), .clr(LoadMap));  // open: en, clk
  consoler CONSOLE_PRINTER (
    .CLK(mainClk), .RESET(letsPrint), .IT_WORKED(InpFl), .INPUT_CHAR(InpKey), .PRINT_SIZE(tpLen),
    .MEM_A(memN), .MEM_D(memChar));
  Register Ypp (.D(maps_1_out_4), .Q(Ypp_q), .clr(LoadMap));  // open: en, clk
  maps maps_1 (
    .ELEM(printing_map_1_curr_adr_in_map), .Width(maps_1_width), .Height(maps_1_height), .DATA(maps_1_data),
    .out_3(maps_1_out_3), .out_4(maps_1_out_4));  // open: ADDR, LEN
  Register #(.width(12)) mapH (.D(maps_1_height), .Q(mapH_q), .clr(LoadMap));  // open: en, clk
  printing_map printing_map_1 (
    .Clock(mainClk), .mem_to_display(printing_map_1_mem_to_display),
    .addr_on_display(printing_map_1_addr_on_display), .Width(mapW_q), .Height(mapH_q),
    .End_of_printing(End_of_printing), .start_Ypp(Ypp_q), .start_Xpp(Xpp_q),
    .curr_adr_in_map(printing_map_1_curr_adr_in_map), .char_from_map(maps_1_data));
  Register #(.width(4)) register_1 (.D(gSto), .Q(gameState), .clk(StateCh), .clr(mainRES));  // open: en
  Comparator #(.width(4)) comparator_1 (.a(4'b0000), .b(gameState), .eq(gS0));  // open: gt, lt
  Comparator #(.width(4)) comparator_2 (.a(4'b0001), .b(gameState), .eq(gS1));  // open: gt, lt
  Comparator #(.width(4)) comparator_3 (.a(4'b0010), .b(gameState), .eq(gS2));  // open: gt, lt
  Register #(.width(1)) register_2 (.D(and_1_out), .Q(register_2_q), .clk(and_1_out), .clr(not_1_out));  // open: en
  and and_1 (and_1_out, InpFl, gS0);
  not not_1 (not_1_out, not_2_out);
  not not_2 (not_2_out, and_1_out);
  buf or_2 (LoadMap, register_2_q);  // OR_Gate
  Register #(.width(1)) register_3 (.D(chGM), .Q(register_3_q), .clk(chGM), .clr(not_4_out));  // open: en
  not not_3 (not_3_out, chGM);
  not not_4 (not_4_out, not_3_out);
  or or_3 (StateCh, register_2_q, register_3_q);
  Multiplexer #(.select(2), .width(4)) multiplexer_1 (
    .in0(4'b0001), .in1(4'b0010), .in2(4'b0001), .out(gSto), .sel({gS2, gS1}));  // open: in3, en
  Multiplexer #(.select(2), .width(8)) multiplexer_2 (
    .in0(8'h1f), .in1({8{1'b0}}), .in2(8'h1e), .out(gStdtScrMem), .sel({gS2, gS1}));  // open: in3, en
  graphic_elems graphic_elems_1 (.ADDR(gStdtScrMem), .ELEM(memN), .DATA(memChar), .LEN(tpLen));
  Button button_2 (.out(chGM));

  // Other names for the same wires on the sheet: memReadyToPrint = in_1

  // Notes on the sheet:
  //   Game state
  //   Дает одиночный короткий импульс 
  //   0 - start screen 1 - walking 2 - atack
  //   1 
  //   1 если прочитан вход
  //   символ входа
  //   Change game mode(... - walkeng - atack - ...)
endmodule

// CP
module consoler (
  input  CLK,
  input  [7:0] MEM_D,
  input  [11:0] PRINT_SIZE,
  input  RESET,
  output IT_WORKED,
  output [7:0] INPUT_CHAR,
  output [11:0] MEM_A
);

  wire adder_1_out, and_3_out, and_4_out, clc, comparator_2_eq, not_1_out, not_2_out, not_3_out, not_4_out,
       not_5_out, or_2_out, PRND, readConsole, register_1_q, register_2_q, RES, RESET_MEMORY_COUNTER_out,
       uart_1_p3, uart_1_p6, uart_1_p8;
  wire [7:0] uart_1_p1;
  wire [11:0] adder_2_out;

  not not_1 (not_1_out, RESET);
  Register #(.width(1)) register_1 (.D(RESET), .Q(register_1_q), .clk(RESET), .clr(not_2_out));  // open: en
  not not_2 (not_2_out, not_1_out);
  and and_1 (clc, CLK, not_3_out);
  not not_3 (not_3_out, RES);
  or or_1 (RES, register_1_q, RESET_MEMORY_COUNTER_out);
  Button RESET_MEMORY_COUNTER (.out(RESET_MEMORY_COUNTER_out));
  and and_2 (IT_WORKED, not_5_out, PRND, register_2_q);
  Register #(.width(1)) register_2 (.D(adder_1_out), .Q(register_2_q), .clk(or_2_out));  // open: en, clr
  or or_2 (or_2_out, RES, uart_1_p3);
  not not_4 (not_4_out, PRND);
  not not_5 (not_5_out, uart_1_p3);
  Adder #(.width(1)) adder_1 (.a(register_2_q), .b(1'b1), .out(adder_1_out));  // open: cin, cout
  Register #(.width(12)) register_3 (.D(adder_2_out), .Q(MEM_A), .clk(and_3_out), .clr(RES));  // open: en
  not not_6 (readConsole, PRND);
  and and_3 (and_3_out, not_4_out, clc);
  Adder #(.width(12)) adder_2 (.a(MEM_A), .b(12'h1), .out(adder_2_out));  // open: cin, cout
  Register register_4 (.D(uart_1_p1), .Q(INPUT_CHAR), .clk(and_4_out), .clr(RES));  // open: en
  and and_4 (and_4_out, clc, comparator_2_eq);
  Comparator #(.width(12)) comparator_1 (.a(MEM_A), .b(PRINT_SIZE), .eq(PRND));  // open: gt, lt
  Comparator comparator_2 (.a(INPUT_CHAR), .b({8{1'b0}}), .eq(comparator_2_eq));  // open: gt, lt
  // UART uart_1: pin names not known; wires that end beside it: uart_1_p1, MEM_D, uart_1_p3, clc, uart_1_p3, uart_1_p6, uart_1_p6, uart_1_p8
  or or_3 (uart_1_p8, uart_1_p3, readConsole);

  // Notes on the sheet:
  //   Frame Printed
  //   Print Frame
  //   Input writened
  //   12 бит адрес
endmodule

// GE
module graphic_elems (
  input  [7:0] ADDR,
  input  [11:0] ELEM,
  output [7:0] DATA,
  output [11:0] LEN
);

  wire [7:0] deMux1, geD0, geD1, geD2, geD2_0, geD2_1, geD3, geD4, geD5, geD6, geD7, geD8, geD9, geD10,
       geD11, geD12, geD13, geD14, geD15;
  wire [11:0] deMuxl1;

  ROM #(.addrWidth(12)) rom_1 (.addr(ELEM), .data(geD0));  // open: sel
  ROM #(.addrWidth(12)) rom_2 (.addr(ELEM), .data(geD1));  // open: sel
  ROM #(.addrWidth(12)) rom_3 (.addr(ELEM), .data(geD2));  // open: sel
  ROM #(.addrWidth(12)) rom_4 (.addr(ELEM), .data(geD3));  // open: sel
  ROM #(.addrWidth(12)) rom_5 (.addr(ELEM), .data(geD4));  // open: sel
  ROM #(.addrWidth(12)) rom_6 (.addr(ELEM), .data(geD5));  // open: sel
  ROM #(.addrWidth(12)) rom_7 (.addr(ELEM), .data(geD6));  // open: sel
  ROM #(.addrWidth(12)) rom_8 (.addr(ELEM), .data(geD7));  // open: sel
  ROM #(.addrWidth(12)) rom_9 (.addr(ELEM), .data(geD8));  // open: sel
  ROM #(.addrWidth(12)) rom_10 (.addr(ELEM), .data(geD9));  // open: sel
  ROM #(.addrWidth(12)) rom_11 (.addr(ELEM), .data(geD10));  // open: sel
  ROM #(.addrWidth(12)) rom_12 (.addr(ELEM), .data(geD11));  // open: sel
  ROM #(.addrWidth(12)) rom_13 (.addr(ELEM), .data(geD12));  // open: sel
  ROM #(.addrWidth(12)) rom_14 (.addr(ELEM), .data(geD13));  // open: sel
  ROM #(.addrWidth(12)) rom_15 (.addr(ELEM), .data(geD14));  // open: sel
  ROM #(.addrWidth(12)) rom_16 (.addr(ELEM), .data(geD15));  // open: sel
  ROM #(.addrWidth(12)) rom_17 (.addr(ELEM), .data(geD2_0));  // open: sel
  ROM #(.addrWidth(12)) rom_18 (.addr(ELEM), .data(geD2_1));  // open: sel
  Multiplexer #(.select(5), .width(8)) multiplexer_1 (
    .in0(geD0), .in1(geD1), .in2(geD2), .in3(geD3), .in4(geD4), .in5(geD5), .in6(geD6), .in7(geD7),
    .in8(geD8), .in9(geD9), .in10(geD10), .in11(geD11), .in12(geD12), .in13(geD13), .in14(geD14),
    .in15(geD15), .in30(geD2_1), .in31(geD2_0), .out(deMux1), .sel(ADDR[4:0]));  // open: in16, in17, in18, in19, in20, in21, in22, in23, in24, in25, in26, in27, in28, in29, en
  Multiplexer #(.select(5), .width(12)) multiplexer_2 (
    .in0(12'had5), .in1(12'h596), .in2(12'h596), .in3(12'h596), .in4(12'h596), .in5(12'h596), .in6(12'h596),
    .in7(12'h596), .in8(12'h596), .in9(12'h596), .in10(12'h596), .in11(12'h596), .in12(12'h596),
    .in13(12'h596), .in14(12'h596), .in15(12'h596), .in30(12'had5), .in31(12'had5), .out(deMuxl1),
    .sel(ADDR[4:0]));  // open: in16, in17, in18, in19, in20, in21, in22, in23, in24, in25, in26, in27, in28, in29, en
  Multiplexer #(.select(3), .width(8)) multiplexer_3 (
    .in0(deMux1), .out(DATA), .sel(ADDR[7:5]));  // open: in1, in2, in3, in4, in5, in6, in7, en
  Multiplexer #(.select(3), .width(12)) multiplexer_4 (
    .in0(deMuxl1), .out(LEN), .sel(ADDR[7:5]));  // open: in1, in2, in3, in4, in5, in6, in7, en

  // Other names for the same wires on the sheet: geAddr1[4:0] = ADDR[4:0]; geAddr2[2:0] = ADDR[7:5];
  //   geEl[11:0] = ELEM

  // Notes on the sheet:
  //   BOARD
  //   contents of rom_1 (hex, n*v repeats v):
  //   0 76*23 a 23 52*20 23 21*20 23 a 23 52*20 23 21*20 23 a 23 52*20 23 21*20 23 a 23 52*20 23 21*20 23
  //   a 23 52*20 23 21*20 23 a 23 52*20 23 21*20 23 a 23 52*20 23 21*20 23 a 23 52*20 23 21*20 23 a 23
  //   52*20 23 21*20 23 a 23 52*20 23 21*20 23 a 23 52*20 23 21*20 23 a 23 52*20 23 21*20 23 a 23 52*20 23
  //   21*20 23 a 23 52*20 23 21*20 23 a 23 52*20 23 21*20 23 a 23 52*20 23 21*20 23 a 23 52*20 23 21*20 23
  //   a 23 52*20 23 21*20 23 a 23 52*20 23 21*20 23 a 23 52*20 23 21*20 23 a 23 52*20 23 21*20 23 a 23
  //   52*20 23*23 a 23 52*20 23 21*20 23 a 23 52*20 23 21*20 23 a 23 52*20 23 21*20 23 a 23 52*20 23 21*20
  //   23 a 23 52*20 23 21*20 23 a 76*23 a 23 74*20 23 a 76*23 a 23 9*20 23 9*20 23 9*20 23 9*20 23 9*20 23
  //   20 48 50 20 7c 10*20 7c 28 20 20 2f 31 30 29 20 23 a 23 9*20 23 9*20 23 9*20 23 9*20 23 9*20 23 20
  //   53 54 20 7c 10*20 7c 28 20 20 2f 31 30 29 20 23 a 23 9*20 23 9*20 23 9*20 23 9*20 23 9*20 23 20 48
  //   47 20 7c 10*20 7c 28 20 20 2f 31 30 29 20 23 a 23 9*20 23 9*20 23 9*20 23 9*20 23 9*20 23 24*20 23 a
  //   76*23 a 52*20
  //   FFL
  //   contents of rom_2 (hex, n*v repeats v):
  //   0 51*20 a 52*20 a 52*20 a 9*20 34*5f 9*20 a 8*20 7c 34*23 7c 8*20 a 8*20 7c 34*23 7c 8*20 a 8*20 7c
  //   34*23 7c 8*20 a 8*20 7c 34*23 7c 8*20 a 8*20 7c 34*23 7c 8*20 a 8*20 7c 34*23 7c 8*20 a 8*20 7c
  //   34*23 7c 8*20 a 8*20 7c 34*23 7c 8*20 a 8*20 7c 34*23 7c 8*20 a 8*20 7c 34*23 7c 8*20 a 8*20 7c
  //   34*23 7c 8*20 a 8*20 7c 34*23 7c 8*20 a 8*20 7c 34*23 7c 8*20 a 8*20 7c 34*23 7c 8*20 a 8*20 7c
  //   34*23 7c 8*20 a 8*20 7c 34*23 7c 8*20 a 8*20 7c 34*23 7c 8*20 a 8*20 7c 34*23 7c 8*20 a 8*20 7c
  //   34*23 7c 8*20 a 52*20 a 52*20 a 52*20 a 52*20
  //   FFFL
  //   contents of rom_3 (hex, n*v repeats v):
  //   0 51*20 a 52*20 a 52*20 a 52*20 a 52*20 a 52*20 a 52*20 a 18*20 16*5f 18*20 a 17*20 7c 16*23 7c
  //   17*20 a 17*20 7c 16*23 7c 17*20 a 17*20 7c 16*23 7c 17*20 a 17*20 7c 16*23 7c 17*20 a 17*20 7c 16*23
  //   7c 17*20 a 17*20 7c 16*23 7c 17*20 a 17*20 7c 16*23 7c 17*20 a 17*20 7c 16*23 7c 17*20 a 17*20 7c
  //   16*23 7c 17*20 a 17*20 7c 16*23 7c 17*20 a 17*20 7c 16*23 7c 17*20 a 52*20 a 52*20 a 52*20 a 52*20 a
  //   52*20 a 52*20 a 52*20 a 52*20
  //   FFFFL
  //   contents of rom_4 (hex, n*v repeats v):
  //   0 51*20 a 52*20 a 52*20 a 52*20 a 52*20 a 52*20 a 52*20 a 52*20 a 52*20 a 52*20 a 24*20 4*5f 24*20 a
  //   23*20 7c 4*23 7c 23*20 a 23*20 7c 4*23 7c 23*20 a 23*20 7c 4*23 7c 23*20 a 23*20 7c 4*23 7c 23*20 a
  //   23*20 7c 4*23 7c 23*20 a 52*20 a 52*20 a 52*20 a 52*20 a 52*20 a 52*20 a 52*20 a 52*20 a 52*20 a
  //   52*20 a 52*20
  //   LFL
  //   contents of rom_5 (hex, n*v repeats v):
  //   0 5c 5f 49*20 a 23 23 5c 5f 48*20 a 4*23 5c 5f 46*20 a 6*23 5c 5f 44*20 a 8*23 7c 43*20 a 8*23 7c
  //   43*20 a 8*23 7c 43*20 a 8*23 7c 43*20 a 8*23 7c 43*20 a 8*23 7c 43*20 a 8*23 7c 43*20 a 8*23 7c
  //   43*20 a 8*23 7c 43*20 a 8*23 7c 43*20 a 8*23 7c 43*20 a 8*23 7c 43*20 a 8*23 7c 43*20 a 8*23 7c
  //   43*20 a 8*23 7c 43*20 a 8*23 7c 43*20 a 8*23 7c 43*20 a 8*23 7c 43*20 a 8*23 7c 43*20 a 6*23 2f
  //   45*20 a 4*23 2f 47*20 a 23 23 2f 49*20 a 2f 51*20
  //   LFFL
  //   contents of rom_6 (hex, n*v repeats v):
  //   0 51*20 a 52*20 a 52*20 a 8*5f 44*20 a 8*23 7c 43*20 a 8*23 7c 43*20 a 8*23 7c 43*20 a 8*23 7c 43*20
  //   a 8*23 7c 43*20 a 8*23 7c 43*20 a 8*23 7c 43*20 a 8*23 7c 43*20 a 8*23 7c 43*20 a 8*23 7c 43*20 a
  //   8*23 7c 43*20 a 8*23 7c 43*20 a 8*23 7c 43*20 a 8*23 7c 43*20 a 8*23 7c 43*20 a 8*23 7c 43*20 a 8*23
  //   7c 43*20 a 8*23 7c 43*20 a 8*23 7c 43*20 a 52*20 a 52*20 a 52*20 a 52*20
  //   LFFFL
  //   contents of rom_7 (hex, n*v repeats v):
  //   0 51*20 a 52*20 a 52*20 a 52*20 a 52*20 a 52*20 a 52*20 a 17*5f 35*20 a 17*23 7c 34*20 a 17*23 7c
  //   34*20 a 17*23 7c 34*20 a 17*23 7c 34*20 a 17*23 7c 34*20 a 17*23 7c 34*20 a 17*23 7c 34*20 a 17*23
  //   7c 34*20 a 17*23 7c 34*20 a 17*23 7c 34*20 a 17*23 7c 34*20 a 52*20 a 52*20 a 52*20 a 52*20 a 52*20
  //   a 52*20 a 52*20 a 52*20
  //   LFFFFL
  //   contents of rom_8 (hex, n*v repeats v):
  //   0 51*20 a 52*20 a 52*20 a 52*20 a 52*20 a 52*20 a 52*20 a 52*20 a 52*20 a 52*20 a 18*20 5*5f 29*20 a
  //   17*20 7c 5*23 7c 28*20 a 17*20 7c 5*23 7c 28*20 a 17*20 7c 5*23 7c 28*20 a 17*20 7c 5*23 7c 28*20 a
  //   17*20 7c 5*23 7c 28*20 a 52*20 a 52*20 a 52*20 a 52*20 a 52*20 a 52*20 a 52*20 a 52*20 a 52*20 a
  //   52*20 a 52*20
  //   RFL
  //   contents of rom_9 (hex, n*v repeats v):
  //   0 50*20 5f 2f a 48*20 5f 2f 23 23 a 46*20 5f 2f 4*23 a 44*20 5f 2f 6*23 a 43*20 7c 8*23 a 43*20 7c
  //   8*23 a 43*20 7c 8*23 a 43*20 7c 8*23 a 43*20 7c 8*23 a 43*20 7c 8*23 a 43*20 7c 8*23 a 43*20 7c 8*23
  //   a 43*20 7c 8*23 a 43*20 7c 8*23 a 43*20 7c 8*23 a 43*20 7c 8*23 a 43*20 7c 8*23 a 43*20 7c 8*23 a
  //   43*20 7c 8*23 a 43*20 7c 8*23 a 43*20 7c 8*23 a 43*20 7c 8*23 a 43*20 7c 8*23 a 45*20 5c 6*23 a
  //   47*20 5c 4*23 a 49*20 5c 23 23 a 51*20 5c
  //   RFFL
  //   contents of rom_10 (hex, n*v repeats v):
  //   0 51*20 a 52*20 a 52*20 a 52*20 a 41*20 5f 2f 7c 8*20 a 39*20 5f 2f 23 23 7c 8*20 a 37*20 5f 2f 4*23
  //   7c 8*20 a 35*20 5f 2f 6*23 7c 8*20 a 34*20 7c 8*23 7c 8*20 a 34*20 7c 8*23 7c 8*20 a 34*20 7c 8*23
  //   7c 8*20 a 34*20 7c 8*23 7c 8*20 a 34*20 7c 8*23 7c 8*20 a 34*20 7c 8*23 7c 8*20 a 34*20 7c 8*23 7c
  //   8*20 a 34*20 7c 8*23 7c 8*20 a 34*20 7c 8*23 7c 8*20 a 34*20 7c 8*23 7c 8*20 a 34*20 7c 8*23 7c 8*20
  //   a 36*20 5c 6*23 7c 8*20 a 38*20 5c 4*23 7c 8*20 a 40*20 5c 23 23 7c 8*20 a 42*20 5c 7c 8*20 a 52*20
  //   a 52*20 a 52*20 a 52*20
  //   RFFFL
  //   contents of rom_11 (hex, n*v repeats v):
  //   0 51*20 a 52*20 a 52*20 a 52*20 a 52*20 a 52*20 a 52*20 a 35*20 17*5f a 34*20 7c 17*23 a 34*20 7c
  //   17*23 a 34*20 7c 17*23 a 34*20 7c 17*23 a 34*20 7c 17*23 a 34*20 7c 17*23 a 34*20 7c 17*23 a 34*20
  //   7c 17*23 a 34*20 7c 17*23 a 34*20 7c 17*23 a 34*20 7c 17*23 a 52*20 a 52*20 a 52*20 a 52*20 a 52*20
  //   a 52*20 a 52*20 a 52*20
  //   RFFFFL
  //   contents of rom_12 (hex, n*v repeats v):
  //   0 51*20 a 52*20 a 52*20 a 52*20 a 52*20 a 52*20 a 52*20 a 52*20 a 52*20 a 52*20 a 29*20 5*5f 18*20 a
  //   28*20 7c 5*23 7c 17*20 a 28*20 7c 5*23 7c 17*20 a 28*20 7c 5*23 7c 17*20 a 28*20 7c 5*23 7c 17*20 a
  //   28*20 7c 5*23 7c 17*20 a 52*20 a 52*20 a 52*20 a 52*20 a 52*20 a 52*20 a 52*20 a 52*20 a 52*20 a
  //   52*20 a 52*20
  //   FRFL
  //   contents of rom_13 (hex, n*v repeats v):
  //   0 51*20 a 52*20 a 52*20 a 52*20 a 41*20 5f 2f 7c 8*20 a 39*20 5f 2f 23 23 7c 8*20 a 37*20 5f 2f 4*23
  //   7c 8*20 a 35*20 5f 2f 6*23 7c 8*20 a 34*20 7c 8*23 7c 8*20 a 34*20 7c 8*23 7c 8*20 a 34*20 7c 8*23
  //   7c 8*20 a 34*20 7c 8*23 7c 8*20 a 34*20 7c 8*23 7c 8*20 a 34*20 7c 8*23 7c 8*20 a 34*20 7c 8*23 7c
  //   8*20 a 34*20 7c 8*23 7c 8*20 a 34*20 7c 8*23 7c 8*20 a 34*20 7c 8*23 7c 8*20 a 34*20 7c 8*23 7c 8*20
  //   a 36*20 5c 6*23 7c 8*20 a 38*20 5c 4*23 7c 8*20 a 40*20 5c 23 23 7c 8*20 a 42*20 5c 7c 8*20 a 52*20
  //   a 52*20 a 52*20 a 52*20
  //   FLFL
  //   contents of rom_14 (hex, n*v repeats v):
  //   0 51*20 a 52*20 a 52*20 a 52*20 a 8*20 7c 5c 5f 41*20 a 8*20 7c 23 23 5c 5f 39*20 a 8*20 7c 4*23 5c
  //   5f 37*20 a 8*20 7c 6*23 5c 5f 35*20 a 8*20 7c 8*23 7c 34*20 a 8*20 7c 8*23 7c 34*20 a 8*20 7c 8*23
  //   7c 34*20 a 8*20 7c 8*23 7c 34*20 a 8*20 7c 8*23 7c 34*20 a 8*20 7c 8*23 7c 34*20 a 8*20 7c 8*23 7c
  //   34*20 a 8*20 7c 8*23 7c 34*20 a 8*20 7c 8*23 7c 34*20 a 8*20 7c 8*23 7c 34*20 a 8*20 7c 8*23 7c
  //   34*20 a 8*20 7c 6*23 2f 36*20 a 8*20 7c 4*23 2f 38*20 a 8*20 7c 23 23 2f 40*20 a 8*20 7c 2f 42*20 a
  //   52*20 a 52*20 a 52*20 a 52*20
  //   FFRFL
  //   contents of rom_15 (hex, n*v repeats v):
  //   0 51*20 a 52*20 a 52*20 a 52*20 a 52*20 a 52*20 a 52*20 a 52*20 a 32*20 5f 2f 7c 17*20 a 30*20 5f 2f
  //   23 23 7c 17*20 a 29*20 2f 4*23 7c 17*20 a 28*20 7c 5*23 7c 17*20 a 28*20 7c 5*23 7c 17*20 a 28*20 7c
  //   5*23 7c 17*20 a 28*20 7c 5*23 7c 17*20 a 28*20 7c 5*23 7c 17*20 a 29*20 5c 4*23 7c 17*20 a 31*20 5c
  //   23 23 7c 17*20 a 33*20 5c 7c 17*20 a 52*20 a 52*20 a 52*20 a 52*20 a 52*20 a 52*20 a 52*20 a 52*20
  //   FFLFL
  //   contents of rom_16 (hex, n*v repeats v):
  //   0 51*20 a 52*20 a 52*20 a 52*20 a 52*20 a 52*20 a 52*20 a 52*20 a 17*20 7c 5c 5f 32*20 a 17*20 7c 23
  //   23 5c 5f 30*20 a 17*20 7c 4*23 5c 29*20 a 17*20 7c 5*23 7c 28*20 a 17*20 7c 5*23 7c 28*20 a 17*20 7c
  //   5*23 7c 28*20 a 17*20 7c 5*23 7c 28*20 a 17*20 7c 5*23 7c 28*20 a 17*20 7c 4*23 2f 29*20 a 17*20 7c
  //   23 23 2f 31*20 a 17*20 7c 2f 33*20 a 52*20 a 52*20 a 52*20 a 52*20 a 52*20 a 52*20 a 52*20 a 52*20
  //   contents of rom_17 (hex, n*v repeats v):
  //   0 76*23 a 23 74*20 23 a 23 74*20 23 a 23 74*20 23 a 23 26*20 5*5f 20 20 5f 40*20 23 a 23 25*20 7c 5f
  //   20 20 20 5f 7c 7c 20 7c 39*20 23 a 23 27*20 7c 20 7c 20 20 7c 20 7c 5f 5f 4*20 5f 5f 5f 30*20 23 a
  //   23 27*20 7c 20 7c 20 20 7c 20 27 5f 20 5c 20 20 2f 20 5f 20 5c 29*20 23 a 23 27*20 7c 20 7c 20 20 7c
  //   20 7c 20 7c 20 7c 7c 20 20 5f 5f 2f 29*20 23 a 23 27*20 5c 5f 2f 20 20 7c 5f 7c 20 7c 5f 7c 20 5c 5f
  //   5f 5f 7c 29*20 23 a 23 20 5f 5f 5f 20 20 5f 5f 5f 8*20 5f 7*20 5f 7*20 5f 40*20 23 a 23 20 7c 20 20
  //   5c 2f 20 20 7c 7*20 7c 20 7c 5*20 28 20 29 5*20 7c 20 7c 39*20 23 a 23 20 7c 20 2e 20 20 2e 20 7c 20
  //   20 5f 5f 5f 20 20 7c 20 7c 20 20 5f 5f 5f 7c 2f 20 5f 5f 5f 20 20 7c 20 7c 5f 5f 20 20 20 5f 20 20
  //   20 5f 20 20 5f 20 5f 5f 20 20 5f 20 5f 5f 20 20 5f 5f 5f 20 5f 5f 6*20 5f 5f 20 23 a 23 20 7c 20 7c
  //   5c 2f 7c 20 7c 20 2f 20 5f 20 5c 20 7c 20 7c 20 2f 20 5f 20 5c 20 2f 20 5f 5f 7c 20 7c 20 27 5f 20
  //   5c 20 7c 20 7c 20 7c 20 7c 7c 20 27 5f 5f 7c 7c 20 27 5f 5f 7c 2f 20 5f 20 5c 5c 20 5c 20 2f 5c 20
  //   2f 20 2f 20 23 a 23 20 7c 20 7c 20 20 7c 20 7c 7c 20 28 5f 29 20 7c 7c 20 7c 7c 20 20 5f 5f 2f 20 5c
  //   5f 5f 20 5c 20 7c 20 7c 5f 29 20 7c 7c 20 7c 5f 7c 20 7c 7c 20 7c 20 20 20 7c 20 7c 20 20 7c 20 28
  //   5f 29 20 7c 5c 20 56 20 20 56 20 2f 20 20 23 a 23 20 5c 5f 7c 20 20 7c 5f 2f 20 5c 5f 5f 5f 2f 20 7c
  //   5f 7c 20 5c 5f 5f 5f 7c 20 7c 5f 5f 5f 2f 20 7c 5f 2e 5f 5f 2f 20 20 5c 5f 5f 2c 5f 7c 7c 5f 7c 20
  //   20 20 7c 5f 7c 20 20 20 5c 5f 5f 5f 2f 20 20 5c 5f 2f 5c 5f 2f 20 20 20 23 a 23 74*20 23 a 23 74*20
  //   23 a 23 74*20 23 a 23 74*20 23 a 23 74*20 23 a 23 74*20 23 a 23 74*20 23 a 23 74*20 23 a 23 74*20 23
  //   a 23 74*20 23 a 23 74*20 23 a 23 74*20 23 a 23 74*20 23 a 23 74*20 23 a 23 74*20 23 a 23 74*20 23 a
  //   23 74*20 23 a 23 39*20 50 52 45 53 53 20 41 4e 59 20 4b 45 59 20 54 4f 20 43 4f 4e 54 49 4e 55 45 2e
  //   2e 2e 7*20 23 a 23 74*20 23 a 76*23 a 52*20
  //   contents of rom_18 (hex, n*v repeats v):
  //   0 76*23 a 23 74*20 23 a 23 74*20 23 a 23 74*20 23 a 23 74*20 23 a 23 74*20 23 a 23 74*20 23 a 23
  //   74*20 23 a 23 74*20 23 a 23 9*20 7c 14*20 7c 13*20 7c 24*20 7c 20 28 20 20 7c 20 20 29 20 20 23 a 23
  //   74*20 23 a 23 74*20 23 a 23 74*20 23 a 23 74*20 23 a 23 74*20 23 a 23 74*20 23 a 23 74*20 23 a 23
  //   74*20 23 a 23 74*20 23 a 23 4*20 65*2d 5*20 23 a 23 74*20 23 a 23 20*20 5e 24*20 2e 28*20 23 a 23
  //   8*20 2e 19*20 2e 10*20 2e 18*20 2e 7*20 2e 7*20 23 a 23 16*20 2e 17*20 2e 17*20 5e 7*20 2e 13*20 23
  //   a 23 23*20 2e 18*20 2e 31*20 23 a 23 6*20 2e 6*20 5e 16*20 5e 23*20 2e 19*20 23 a 23 23*20 2e 11*20
  //   2e 5*20 2e 20*20 5e 11*20 23 a 23 74*20 23 a 76*23 a 23 74*20 23 a 76*23 a 23 9*20 23 9*20 23 9*20
  //   23 9*20 23 9*20 23 20 48 50 20 7c 10*20 7c 28 20 20 2f 31 30 29 20 23 a 23 9*20 23 9*20 23 9*20 23
  //   9*20 23 9*20 23 20 53 54 20 7c 10*20 7c 28 20 20 2f 31 30 29 20 23 a 23 9*20 23 9*20 23 9*20 23 9*20
  //   23 9*20 23 20 48 47 20 7c 10*20 7c 28 20 20 2f 31 30 29 20 23 a 23 9*20 23 9*20 23 9*20 23 9*20 23
  //   9*20 23 24*20 23 a 76*23 a 52*20
  //   START SCREEN
  //   ATACK BOARD
endmodule

// Maps
module maps (
  input  [7:0] ADDR,
  input  [11:0] ELEM,
  output [7:0] out_3,
  output [7:0] out_4,
  output [11:0] LEN,
  output [7:0] DATA,
  output [11:0] Width,
  output [11:0] Height
);

  wire [7:0] mgeD0, undriven_4, undriven_5;
  wire [11:0] undriven, undriven_2, undriven_3;

  ROM #(.addrWidth(12)) rom_1 (.addr(ELEM), .data(mgeD0), .sel(1'b1));
  Multiplexer #(.select(5), .width(12)) multiplexer_1 (
    .in0(12'h49), .in30(undriven), .in31(undriven), .out(LEN), .sel(ADDR[4:0]));  // open: in1, in2, in3, in4, in5, in6, in7, in8, in9, in10, in11, in12, in13, in14, in15, in16, in17, in18, in19, in20, in21, in22, in23, in24, in25, in26, in27, in28, in29, en
  Multiplexer #(.select(5), .width(8)) multiplexer_2 (
    .in0(mgeD0), .out(DATA), .sel(ADDR[4:0]));  // open: in1, in2, in3, in4, in5, in6, in7, in8, in9, in10, in11, in12, in13, in14, in15, in16, in17, in18, in19, in20, in21, in22, in23, in24, in25, in26, in27, in28, in29, in30, in31, en
  // Probe on LEN
  // Probe on Width
  Multiplexer #(.select(5), .width(12)) multiplexer_3 (
    .in0(12'hc), .in30(undriven_2), .in31(undriven_2), .out(Width), .sel(ADDR[4:0]));  // open: in1, in2, in3, in4, in5, in6, in7, in8, in9, in10, in11, in12, in13, in14, in15, in16, in17, in18, in19, in20, in21, in22, in23, in24, in25, in26, in27, in28, in29, en
  // Probe on Height
  Multiplexer #(.select(5), .width(12)) multiplexer_4 (
    .in0(12'hc), .in30(undriven_3), .in31(undriven_3), .out(Height), .sel(ADDR[4:0]));  // open: in1, in2, in3, in4, in5, in6, in7, in8, in9, in10, in11, in12, in13, in14, in15, in16, in17, in18, in19, in20, in21, in22, in23, in24, in25, in26, in27, in28, in29, en
  Multiplexer #(.select(5), .width(8)) multiplexer_5 (
    .in0(8'h5), .in30(undriven_4), .in31(undriven_4), .out(out_4), .sel(ADDR[4:0]));  // open: in1, in2, in3, in4, in5, in6, in7, in8, in9, in10, in11, in12, in13, in14, in15, in16, in17, in18, in19, in20, in21, in22, in23, in24, in25, in26, in27, in28, in29, en
  Multiplexer #(.select(5), .width(8)) multiplexer_6 (
    .in0(8'h5), .in30(undriven_5), .in31(undriven_5), .out(out_3), .sel(ADDR[4:0]));  // open: in1, in2, in3, in4, in5, in6, in7, in8, in9, in10, in11, in12, in13, in14, in15, in16, in17, in18, in19, in20, in21, in22, in23, in24, in25, in26, in27, in28, in29, en

  // Other names for the same wires on the sheet: mdeMux1[7:0] = DATA; mdeMuxl1[11:0] = LEN; mgeAddr1[4:0] = ADDR[4:0];
  //   mgeEl[11:0] = ELEM; mhMuxl1[11:0] = Height; mhMuxlX[7:0] = out_3; mwMuxl1[11:0] = Width; mwMuxlY[7:0] = out_4

  // Notes on the sheet:
  //   TEST MAP
  //   contents of rom_1 (hex, n*v repeats v):
  //   40*23 20 23 20 20 20 7*23 20 23 20 23 20 6*23 20 20 50 20 23 20 6*23 20 23 4*20 6*23 20 23 23 20
  //   8*23 20 20 23 20 20 20 39*23
endmodule

module printing_map (
  input  [7:0] char_from_map,
  input  [7:0] start_Ypp,
  input  [7:0] start_Xpp,
  input  Clock,
  input  [11:0] Width,
  input  [11:0] Height,
  output [11:0] curr_adr_in_map,
  output End_of_printing,
  output [7:0] mem_to_display,
  output [11:0] addr_on_display
);

  wire and_1_out, and_2_out, and_3_out, and_4_out, comparator_2_lt, comparator_4_lt, comparator_5_lt,
       not_1_out, or_2_out, or_3_out, or_4_out, or_5_out, X____Y____0;
  wire [7:0] or_1_out;
  wire [11:0] adder_1_out, adder_2_out, adder_3_out, adder_4_out, adder_5_out, adder_6_out, adder_7_out,
       adder_8_out, adder_10_out, adder_11_out, adder_13_out, curr_addr_on_display, multiplier_1_out,
       multiplier_2_out, register_1_q, register_2_q, register_3_q, register_4_q;

  // Probe on Width
  // Probe on char_from_map
  // Probe on addr_on_display
  assign addr_on_display = not_1_out ? curr_addr_on_display : 12'bz;  // Controlled_Buffer controlled_buffer_1
  not not_1 (not_1_out, X____Y____0);
  // Probe on Height
  ROM #(.addrWidth(12)) rom_1 (.sel(1'b1));  // open: addr, data
  assign or_1_out = start_Ypp | start_Xpp;  // OR_Gate or_1, 8 bits wide
  Comparator comparator_1 (.a(or_1_out), .b({8{1'b0}}), .eq(X____Y____0));  // open: gt, lt
  Register #(.width(12)) register_1 (.D(adder_2_out), .Q(register_1_q), .clk(and_1_out), .clr(or_2_out));  // open: en
  and and_1 (and_1_out, Clock, comparator_4_lt);
  Adder #(.width(12)) adder_1 (.a(12'hffd), .b(register_1_q), .out(adder_1_out));  // open: cin, cout
  Adder #(.width(12)) adder_2 (.a(register_1_q), .b(12'h1), .out(adder_2_out));  // open: cin, cout
  or or_2 (or_2_out, End_of_printing, comparator_2_lt);
  Adder #(.width(12)) adder_3 (.a({4'b0000, start_Ypp}), .b(adder_1_out), .out(adder_3_out));  // open: cin, cout
  Comparator #(.width(12), .mode("unsigned")) comparator_2 (
    .a(12'h6), .b(register_1_q), .lt(comparator_2_lt));  // open: gt, eq
  Register #(.width(12)) register_2 (.D(adder_4_out), .Q(register_2_q), .clk(and_2_out), .clr(or_3_out));  // open: en
  and and_2 (and_2_out, Clock, comparator_5_lt);
  or or_3 (or_3_out, End_of_printing, End_of_printing);
  Multiplier #(.width(12)) multiplier_1 (.a(12'h4f), .b(register_2_q), .out(multiplier_1_out));  // open: cin, cout
  Adder #(.width(12)) adder_4 (.a(register_2_q), .b(12'h1), .out(adder_4_out));  // open: cin, cout
  Adder #(.width(12)) adder_5 (.a(12'h3), .b(multiplier_2_out), .out(adder_5_out));  // open: cin, cout
  Multiplier #(.width(12)) multiplier_2 (.a(Width), .b(adder_3_out), .out(multiplier_2_out));  // open: cin, cout
  // Probe on multiplier_2_out
  Adder #(.width(12)) adder_6 (.a(12'h4f), .b(multiplier_1_out), .out(adder_6_out));  // open: cin, cout
  Comparator #(.width(12), .mode("unsigned")) comparator_3 (
    .a(12'h6), .b(register_2_q), .lt(End_of_printing));  // open: gt, eq
  Adder #(.width(12)) adder_7 (.a(adder_5_out), .b(adder_8_out), .out(adder_7_out));  // open: cin, cout
  Adder #(.width(12)) adder_8 (.a(12'hffd), .b(adder_10_out), .out(adder_8_out));  // open: cin, cout
  Register #(.width(12)) register_3 (.D(adder_10_out), .Q(register_3_q), .clk(and_3_out), .clr(or_4_out));  // open: en
  and and_3 (and_3_out, Clock, ~X____Y____0);  // AND_Gate
  or or_4 (or_4_out, End_of_printing, comparator_4_lt);
  Adder #(.width(12)) adder_9 (.a({4'b0000, start_Xpp}), .b(adder_7_out), .out(curr_adr_in_map));  // open: cin, cout
  Comparator #(.width(12), .mode("unsigned")) comparator_4 (
    .a(12'h6), .b(register_3_q), .lt(comparator_4_lt));  // open: gt, eq
  Adder #(.width(12)) adder_10 (.a(register_3_q), .b(12'h1), .out(adder_10_out));  // open: cin, cout
  Adder #(.width(12)) adder_11 (.a(adder_6_out), .b(12'h36), .out(adder_11_out));  // open: cin, cout
  and and_4 (and_4_out, Clock, ~X____Y____0);  // AND_Gate
  // Probe on curr_adr_in_map
  Register #(.width(12)) register_4 (.D(adder_13_out), .Q(register_4_q), .clk(and_4_out), .clr(or_5_out));  // open: en
  or or_5 (or_5_out, End_of_printing, comparator_5_lt);
  Adder #(.width(12)) adder_12 (.a(adder_11_out), .b(register_4_q), .out(curr_addr_on_display));  // open: cin, cout
  Comparator #(.width(12), .mode("unsigned")) comparator_5 (
    .a(12'h6), .b(register_4_q), .lt(comparator_5_lt));  // open: gt, eq
  Adder #(.width(12)) adder_13 (.a(register_4_q), .b(12'h1), .out(adder_13_out));  // open: cin, cout

  assign mem_to_display = char_from_map;

  // Other names for the same wires on the sheet: curr_y[7:0] = start_Ypp; start_y[7:0] = start_Ypp;
  //   curr_x[7:0] = start_Xpp; start_x[7:0] = start_Xpp; curr_addr_on_map[11:0] = curr_adr_in_map;
  //   Curr_char[7:0] = char_from_map; End = End_of_printing

  // Notes on the sheet:
  //   contents of rom_1 (hex, n*v repeats v):
  //   0 5 5 2 40*23 20 23 20 20 20 7*23 20 23 20 23 20 6*23 20 20 50 20 23 20 6*23 20 23 4*20 6*23 20 23
  //   23 20 8*23 20 20 23 20 20 20 39*23
endmodule

module \То__что_не_пригодилось  (
  input  in_1
);

  wire and_1_out, and_3_out, and_4_out, and_5_out, comparator_1_lt, comparator_2_eq, comparator_3_eq,
       comparator_4_eq, comparator_5_eq, comparator_6_eq, comparator_6_lt, comparator_7_lt, comparator_8_eq,
       comparator_8_lt, cond_of_end_consts, not_1_out, not_2_out, not_3_out, not_4_out, x____y;
  wire [7:0] _8_bit_NULL, curr_map_char, curr_x, curr_y;
  wire [11:0] adder_1_out, adder_2_out, adder_3_out, adder_5_out, adder_6_out, adder_7_out, adder_8_out,
       adder_9_out, controlled_buffer_1_out, controlled_buffer_3_out, controlled_buffer_5_out,
       controlled_buffer_7_out, controlled_buffer_8_out, controlled_buffer_9_out, controlled_buffer_10_out,
       controlled_buffer_11_out, Curr_Adress, height, multiplier_1_out, multiplier_2_out,
       pull_resistor_1_node, register_1_q, register_2_q, register_4_q, register_5_q, width;

  assign controlled_buffer_1_out = cond_of_end_consts ? controlled_buffer_3_out : 12'bz;  // Controlled_Buffer controlled_buffer_1
  not not_1 (not_1_out, cond_of_end_consts);
  assign controlled_buffer_1_out = not_1_out ? 12'h1 : 12'bz;  // Controlled_Buffer controlled_buffer_2
  Register #(.width(12)) register_1 (
    .D(controlled_buffer_1_out), .Q(register_1_q), .clk(and_1_out), .clr(comparator_1_lt));  // open: en
  and and_1 (and_1_out, in_1, ~x____y, cond_of_end_consts);  // AND_Gate
  assign controlled_buffer_3_out = not_2_out ? register_1_q : 12'bz;  // Controlled_Buffer controlled_buffer_3
  Adder #(.width(12)) adder_1 (.a(register_1_q), .b(12'h1), .out(adder_1_out));  // open: cin, cout
  Comparator #(.width(12), .mode("unsigned")) comparator_1 (
    .a(height), .b(controlled_buffer_3_out), .lt(comparator_1_lt));  // open: gt, eq
  assign controlled_buffer_3_out = comparator_6_eq ? adder_1_out : 12'bz;  // Controlled_Buffer controlled_buffer_4
  not not_2 (not_2_out, comparator_6_eq);
  Comparator comparator_2 (.a(_8_bit_NULL), .b(controlled_buffer_3_out[7:0]), .eq(comparator_2_eq));  // open: gt, lt
  Comparator #(.mode("unsigned")) comparator_3 (
    .a(curr_y), .b(controlled_buffer_3_out[7:0]), .eq(comparator_3_eq));  // open: gt, lt
  not not_3 (not_3_out, cond_of_end_consts);
  assign controlled_buffer_5_out = not_3_out ? 12'h1 : 12'bz;  // Controlled_Buffer controlled_buffer_5
  and and_2 (x____y, ~comparator_2_eq, comparator_3_eq, comparator_4_eq, ~comparator_5_eq);  // AND_Gate
  assign controlled_buffer_5_out = cond_of_end_consts ? adder_2_out : 12'bz;  // Controlled_Buffer controlled_buffer_6
  Register #(.width(12)) register_2 (
    .D(controlled_buffer_5_out), .Q(register_2_q), .clk(and_3_out), .clr(comparator_6_lt));  // open: en
  and and_3 (and_3_out, in_1, ~x____y, cond_of_end_consts);  // AND_Gate
  Comparator #(.mode("unsigned")) comparator_4 (
    .a(curr_x), .b(register_2_q[7:0]), .eq(comparator_4_eq));  // open: gt, lt
  Adder #(.width(12)) adder_2 (.a(register_2_q), .b(12'h1), .out(adder_2_out));  // open: cin, cout
  Comparator comparator_5 (.a(_8_bit_NULL), .b(register_2_q[7:0]), .eq(comparator_5_eq));  // open: gt, lt
  Comparator #(.width(12), .mode("unsigned")) comparator_6 (
    .a(width), .b(register_2_q), .eq(comparator_6_eq), .lt(comparator_6_lt));  // open: gt
  Register register_3 (.Q(curr_map_char), .clk(in_1));  // open: D, en, clr
  assign controlled_buffer_7_out = x____y ? Curr_Adress : 12'bz;  // Controlled_Buffer controlled_buffer_7
  Adder #(.width(12)) adder_3 (
    .a(controlled_buffer_7_out), .b(controlled_buffer_8_out), .out(adder_3_out));  // open: cin, cout
  assign controlled_buffer_8_out = x____y ? 12'hffc : 12'bz;  // Controlled_Buffer controlled_buffer_8
  assign controlled_buffer_9_out = x____y ? width : 12'bz;  // Controlled_Buffer controlled_buffer_9
  Multiplier #(.width(12)) multiplier_1 (
    .a(controlled_buffer_9_out), .b(controlled_buffer_10_out), .out(multiplier_1_out));  // open: cin, cout
  assign controlled_buffer_10_out = x____y ? 12'hffd : 12'bz;  // Controlled_Buffer controlled_buffer_10
  Pull_Resistor pull_resistor_1 (.node(pull_resistor_1_node[0]));
  Pull_Resistor pull_resistor_2 (.node(pull_resistor_1_node[1]));
  Pull_Resistor pull_resistor_3 (.node(pull_resistor_1_node[2]));
  Pull_Resistor pull_resistor_4 (.node(pull_resistor_1_node[3]));
  Pull_Resistor pull_resistor_5 (.node(pull_resistor_1_node[4]));
  Pull_Resistor pull_resistor_6 (.node(pull_resistor_1_node[5]));
  Pull_Resistor pull_resistor_7 (.node(pull_resistor_1_node[6]));
  Pull_Resistor pull_resistor_8 (.node(pull_resistor_1_node[7]));
  Pull_Resistor pull_resistor_9 (.node(pull_resistor_1_node[8]));
  Pull_Resistor pull_resistor_10 (.node(pull_resistor_1_node[9]));
  Pull_Resistor pull_resistor_11 (.node(pull_resistor_1_node[10]));
  Pull_Resistor pull_resistor_12 (.node(pull_resistor_1_node[11]));
  // Probe on multiplier_1_out
  // Probe on pull_resistor_1_node
  Adder #(.width(12)) adder_4 (.a(adder_3_out), .b(multiplier_1_out), .out(pull_resistor_1_node));  // open: cin, cout
  Register #(.width(12)) register_4 (
    .D(controlled_buffer_11_out), .Q(register_4_q), .clk(and_4_out), .clr(comparator_7_lt));  // open: en
  and and_4 (and_4_out, in_1, x____y);
  Multiplier #(.width(12)) multiplier_2 (
    .a(width), .b(controlled_buffer_11_out), .out(multiplier_2_out));  // open: cin, cout
  assign controlled_buffer_11_out = not_4_out ? register_4_q : 12'bz;  // Controlled_Buffer controlled_buffer_11
  Adder #(.width(12)) adder_5 (.a(register_4_q), .b(12'h1), .out(adder_5_out));  // open: cin, cout
  Adder #(.width(12)) adder_6 (.a(pull_resistor_1_node), .b(multiplier_2_out), .out(adder_6_out));  // open: cin, cout
  Comparator #(.width(12), .mode("unsigned")) comparator_7 (
    .a(height), .b(controlled_buffer_11_out), .lt(comparator_7_lt));  // open: gt, eq
  assign controlled_buffer_11_out = comparator_8_eq ? adder_5_out : 12'bz;  // Controlled_Buffer controlled_buffer_12
  not not_4 (not_4_out, comparator_8_eq);
  Adder #(.width(12)) adder_7 (.a(adder_6_out), .b(adder_8_out), .out(adder_7_out));  // open: cin, cout
  Adder #(.width(12)) adder_8 (.a(12'hffe), .b(adder_9_out), .out(adder_8_out));  // open: cin, cout
  Register #(.width(12)) register_5 (
    .D(adder_9_out), .Q(register_5_q), .clk(and_5_out), .clr(comparator_8_lt));  // open: en
  and and_5 (and_5_out, in_1, x____y);
  // Probe on adder_7_out
  Adder #(.width(12)) adder_9 (.a(register_5_q), .b(12'h1), .out(adder_9_out));  // open: cin, cout
  Comparator #(.width(12), .mode("unsigned")) comparator_8 (
    .a(width), .b(register_5_q), .eq(comparator_8_eq), .lt(comparator_8_lt));  // open: gt

  // Other names for the same wires on the sheet: Clock = in_1
endmodule
